// Logisim project COUNT_DISPLAY_Student1.circ as structural Verilog: 1 circuit
module COUNT_DISPLAY (
);

  // Pin S3: pin names not known
  // Pin S2: pin names not known
  // Pin S1: pin names not known
  // Pin S0: pin names not known
  // Pin N2: pin names not known
  // Pin N1: pin names not known
  // Pin N0: pin names not known
endmodule
